// Logisim project connect4.circ as structural Verilog: 6 circuits, main circuit main
module main (
);

  wire _1_2_out, _1_3_out, _1_out, _2_2_out, _2_3_out, _2_out, _3_2_out, _3_3_out, _3_out, _4_2_out,
       _4_3_out, _4_out, _5_2_out, _5_3_out, _5_out, _6_2_out, _6_3_out, _6_out, _7_2_out, _7_3_out, _7_out,
       and_1_out, and_2_out, and_3_out, and_4_out, and_5_out, and_6_out, and_7_out, and_8_out, and_9_out,
       and_10_out, and_11_out, and_12_out, and_13_out, and_14_out, column_1_p1r0, column_1_p1r1,
       column_1_p1r2, column_1_p1r3, column_1_p1r4, column_1_p1r5, column_1_p1r6, column_1_p2r0,
       column_1_p2r1, column_1_p2r2, column_1_p2r3, column_1_p2r4, column_1_p2r5, column_1_p2r6,
       column_2_p1r0, column_2_p1r1, column_2_p1r2, column_2_p1r3, column_2_p1r4, column_2_p1r5,
       column_2_p1r6, column_2_p2r0, column_2_p2r1, column_2_p2r2, column_2_p2r3, column_2_p2r4,
       column_2_p2r5, column_2_p2r6, column_3_p1r0, column_3_p1r1, column_3_p1r2, column_3_p1r3,
       column_3_p1r4, column_3_p1r5, column_3_p1r6, column_3_p2r0, column_3_p2r1, column_3_p2r2,
       column_3_p2r3, column_3_p2r4, column_3_p2r5, column_3_p2r6, column_4_p1r0, column_4_p1r1,
       column_4_p1r2, column_4_p1r3, column_4_p1r4, column_4_p1r5, column_4_p1r6, column_4_p2r0,
       column_4_p2r1, column_4_p2r2, column_4_p2r3, column_4_p2r4, column_4_p2r5, column_4_p2r6,
       column_5_p1r0, column_5_p1r1, column_5_p1r2, column_5_p1r3, column_5_p1r4, column_5_p1r5,
       column_5_p1r6, column_5_p2r0, column_5_p2r1, column_5_p2r2, column_5_p2r3, column_5_p2r4,
       column_5_p2r5, column_5_p2r6, column_6_p1r0, column_6_p1r1, column_6_p1r2, column_6_p1r3,
       column_6_p1r4, column_6_p1r5, column_6_p1r6, column_6_p2r0, column_6_p2r1, column_6_p2r2,
       column_6_p2r3, column_6_p2r4, column_6_p2r5, column_6_p2r6, column_7_p1r0, column_7_p1r1,
       column_7_p1r2, column_7_p1r3, column_7_p1r4, column_7_p1r5, column_7_p1r6, column_7_p2r0,
       column_7_p2r1, column_7_p2r2, column_7_p2r3, column_7_p2r4, column_7_p2r5, column_7_p2r6, or_1_out,
       or_2_out, or_3_out, sr_flip_flop_1_minus_q, sr_flip_flop_1_q, Start_out;

  Button _2 (.out(_2_out));
  Button _1 (.out(_1_out));
  and and_1 (and_1_out, _1_out, sr_flip_flop_1_q);
  Button _4 (.out(_4_out));
  Button _3 (.out(_3_out));
  and and_2 (and_2_out, _4_out, sr_flip_flop_1_q);
  and and_3 (and_3_out, _2_out, sr_flip_flop_1_q);
  and and_4 (and_4_out, _3_out, sr_flip_flop_1_q);
  Button _5 (.out(_5_out));
  Button _7 (.out(_7_out));
  Button _6 (.out(_6_out));
  and and_5 (and_5_out, _6_out, sr_flip_flop_1_q);
  and and_6 (and_6_out, _7_out, sr_flip_flop_1_q);
  and and_7 (and_7_out, _5_out, sr_flip_flop_1_q);
  Column column_1 (
    .p1r6(column_1_p1r6), .p2r6(column_1_p2r6), .p1r5(column_1_p1r5), .p2r5(column_1_p2r5),
    .p1r4(column_1_p1r4), .p2r4(column_1_p2r4), .p1r3(column_1_p1r3), .p2r3(column_1_p2r3),
    .p1r2(column_1_p1r2), .p2r2(column_1_p2r2), .p1r1(column_1_p1r1), .p2r1(column_1_p2r1),
    .p1r0(column_1_p1r0), .p2r0(column_1_p2r0), .clock(_1_2_out), .reset(Start_out),
    .player_2(sr_flip_flop_1_q), .player_1(sr_flip_flop_1_minus_q));
  LED led_1 (.in(column_2_p1r6));
  LED led_2 (.in(column_1_p1r6));
  LED led_3 (.in(column_1_p2r6));
  LED led_4 (.in(column_1_p1r5));
  LED led_5 (.in(column_2_p1r5));
  LED led_6 (.in(column_1_p2r5));
  LED led_7 (.in(column_2_p1r4));
  LED led_8 (.in(column_1_p1r4));
  LED led_9 (.in(column_1_p2r4));
  LED led_10 (.in(column_2_p1r3));
  LED led_11 (.in(column_1_p1r3));
  LED led_12 (.in(column_1_p2r3));
  LED led_13 (.in(column_1_p1r2));
  LED led_14 (.in(column_2_p1r2));
  LED led_15 (.in(column_1_p2r2));
  LED led_16 (.in(column_2_p1r1));
  LED led_17 (.in(column_1_p1r1));
  LED led_18 (.in(column_1_p2r1));
  LED led_19 (.in(column_2_p1r0));
  LED led_20 (.in(column_1_p1r0));
  LED led_21 (.in(column_1_p2r0));
  or _1_2 (_1_2_out, and_1_out, and_8_out);
  LED led_22 (.in(sr_flip_flop_1_q));
  or or_1 (or_1_out, and_6_out, and_5_out, and_7_out, and_2_out, and_4_out, and_3_out, and_1_out);
  LED led_23 (.in(column_3_p1r6));
  Column column_2 (
    .p1r6(column_2_p1r6), .p2r6(column_2_p2r6), .p1r5(column_2_p1r5), .p2r5(column_2_p2r5),
    .p1r4(column_2_p1r4), .p2r4(column_2_p2r4), .p1r3(column_2_p1r3), .p2r3(column_2_p2r3),
    .p1r2(column_2_p1r2), .p2r2(column_2_p2r2), .p1r1(column_2_p1r1), .p2r1(column_2_p2r1),
    .p1r0(column_2_p1r0), .p2r0(column_2_p2r0), .clock(_2_2_out), .reset(Start_out),
    .player_2(sr_flip_flop_1_q), .player_1(sr_flip_flop_1_minus_q));
  LED led_24 (.in(column_3_p2r6));
  LED led_25 (.in(column_2_p2r6));
  LED led_26 (.in(column_3_p1r5));
  LED led_27 (.in(column_3_p2r5));
  LED led_28 (.in(column_2_p2r5));
  LED led_29 (.in(column_3_p1r4));
  LED led_30 (.in(column_2_p2r4));
  LED led_31 (.in(column_3_p2r4));
  LED led_32 (.in(column_3_p1r3));
  LED led_33 (.in(column_3_p2r3));
  LED led_34 (.in(column_2_p2r3));
  LED led_35 (.in(column_3_p1r2));
  LED led_36 (.in(column_3_p2r2));
  LED led_37 (.in(column_2_p2r2));
  LED led_38 (.in(column_3_p1r1));
  LED led_39 (.in(column_2_p2r1));
  LED led_40 (.in(column_3_p2r1));
  LED led_41 (.in(column_3_p1r0));
  LED led_42 (.in(column_2_p2r0));
  LED led_43 (.in(column_3_p2r0));
  or _3_2 (_3_2_out, and_4_out, and_10_out);
  or _2_2 (_2_2_out, and_3_out, and_9_out);
  Button Start (.out(Start_out));
  or or_2 (or_2_out, Start_out, or_3_out);
  SR_Flip_Flop sr_flip_flop_1 (.R(or_1_out), .S(or_2_out), .Q(sr_flip_flop_1_q), .minus_Q(sr_flip_flop_1_minus_q));
  Column column_3 (
    .p1r6(column_3_p1r6), .p2r6(column_3_p2r6), .p1r5(column_3_p1r5), .p2r5(column_3_p2r5),
    .p1r4(column_3_p1r4), .p2r4(column_3_p2r4), .p1r3(column_3_p1r3), .p2r3(column_3_p2r3),
    .p1r2(column_3_p1r2), .p2r2(column_3_p2r2), .p1r1(column_3_p1r1), .p2r1(column_3_p2r1),
    .p1r0(column_3_p1r0), .p2r0(column_3_p2r0), .clock(_3_2_out), .reset(Start_out),
    .player_2(sr_flip_flop_1_q), .player_1(sr_flip_flop_1_minus_q));
  LED led_44 (.in(column_4_p1r6));
  Column column_4 (
    .p1r6(column_4_p1r6), .p2r6(column_4_p2r6), .p1r5(column_4_p1r5), .p2r5(column_4_p2r5),
    .p1r4(column_4_p1r4), .p2r4(column_4_p2r4), .p1r3(column_4_p1r3), .p2r3(column_4_p2r3),
    .p1r2(column_4_p1r2), .p2r2(column_4_p2r2), .p1r1(column_4_p1r1), .p2r1(column_4_p2r1),
    .p1r0(column_4_p1r0), .p2r0(column_4_p2r0), .clock(_4_2_out), .reset(Start_out),
    .player_2(sr_flip_flop_1_q), .player_1(sr_flip_flop_1_minus_q));
  LED led_45 (.in(column_5_p1r6));
  LED led_46 (.in(column_4_p2r6));
  LED led_47 (.in(column_5_p1r5));
  LED led_48 (.in(column_4_p1r5));
  LED led_49 (.in(column_4_p2r5));
  LED led_50 (.in(column_4_p1r4));
  LED led_51 (.in(column_5_p1r4));
  LED led_52 (.in(column_4_p2r4));
  LED led_53 (.in(column_5_p1r3));
  LED led_54 (.in(column_4_p1r3));
  LED led_55 (.in(column_4_p2r3));
  LED led_56 (.in(column_4_p1r2));
  LED led_57 (.in(column_5_p1r2));
  LED led_58 (.in(column_4_p2r2));
  LED led_59 (.in(column_4_p1r1));
  LED led_60 (.in(column_5_p1r1));
  LED led_61 (.in(column_4_p2r1));
  LED led_62 (.in(column_5_p1r0));
  LED led_63 (.in(column_4_p1r0));
  LED led_64 (.in(column_4_p2r0));
  or _4_2 (_4_2_out, and_2_out, and_11_out);
  LED led_65 (.in(sr_flip_flop_1_minus_q));
  or or_3 (or_3_out, and_13_out, and_14_out, and_12_out, and_11_out, and_10_out, and_9_out, and_8_out);
  LED led_66 (.in(column_6_p1r6));
  Column column_5 (
    .p1r6(column_5_p1r6), .p2r6(column_5_p2r6), .p1r5(column_5_p1r5), .p2r5(column_5_p2r5),
    .p1r4(column_5_p1r4), .p2r4(column_5_p2r4), .p1r3(column_5_p1r3), .p2r3(column_5_p2r3),
    .p1r2(column_5_p1r2), .p2r2(column_5_p2r2), .p1r1(column_5_p1r1), .p2r1(column_5_p2r1),
    .p1r0(column_5_p1r0), .p2r0(column_5_p2r0), .clock(_5_2_out), .reset(Start_out),
    .player_2(sr_flip_flop_1_q), .player_1(sr_flip_flop_1_minus_q));
  Column column_6 (
    .p1r6(column_6_p1r6), .p2r6(column_6_p2r6), .p1r5(column_6_p1r5), .p2r5(column_6_p2r5),
    .p1r4(column_6_p1r4), .p2r4(column_6_p2r4), .p1r3(column_6_p1r3), .p2r3(column_6_p2r3),
    .p1r2(column_6_p1r2), .p2r2(column_6_p2r2), .p1r1(column_6_p1r1), .p2r1(column_6_p2r1),
    .p1r0(column_6_p1r0), .p2r0(column_6_p2r0), .clock(_6_2_out), .reset(Start_out),
    .player_2(sr_flip_flop_1_q), .player_1(sr_flip_flop_1_minus_q));
  LED led_67 (.in(column_6_p2r6));
  LED led_68 (.in(column_5_p2r6));
  LED led_69 (.in(column_6_p1r5));
  LED led_70 (.in(column_6_p2r5));
  LED led_71 (.in(column_5_p2r5));
  LED led_72 (.in(column_6_p1r4));
  LED led_73 (.in(column_5_p2r4));
  LED led_74 (.in(column_6_p2r4));
  LED led_75 (.in(column_6_p1r3));
  LED led_76 (.in(column_5_p2r3));
  LED led_77 (.in(column_6_p2r3));
  LED led_78 (.in(column_6_p1r2));
  LED led_79 (.in(column_6_p2r2));
  LED led_80 (.in(column_5_p2r2));
  LED led_81 (.in(column_6_p1r1));
  LED led_82 (.in(column_6_p2r1));
  LED led_83 (.in(column_5_p2r1));
  LED led_84 (.in(column_6_p1r0));
  LED led_85 (.in(column_6_p2r0));
  LED led_86 (.in(column_5_p2r0));
  or _5_2 (_5_2_out, and_7_out, and_12_out);
  or _6_2 (_6_2_out, and_5_out, and_14_out);
  Button _2_3 (.out(_2_3_out));
  Button _3_3 (.out(_3_3_out));
  Button _1_3 (.out(_1_3_out));
  and and_8 (and_8_out, _1_3_out, sr_flip_flop_1_minus_q);
  and and_9 (and_9_out, _2_3_out, sr_flip_flop_1_minus_q);
  and and_10 (and_10_out, _3_3_out, sr_flip_flop_1_minus_q);
  Column column_7 (
    .p1r6(column_7_p1r6), .p2r6(column_7_p2r6), .p1r5(column_7_p1r5), .p2r5(column_7_p2r5),
    .p1r4(column_7_p1r4), .p2r4(column_7_p2r4), .p1r3(column_7_p1r3), .p2r3(column_7_p2r3),
    .p1r2(column_7_p1r2), .p2r2(column_7_p2r2), .p1r1(column_7_p1r1), .p2r1(column_7_p2r1),
    .p1r0(column_7_p1r0), .p2r0(column_7_p2r0), .clock(_7_2_out), .reset(Start_out),
    .player_2(sr_flip_flop_1_q), .player_1(sr_flip_flop_1_minus_q));
  LED led_87 (.in(column_7_p1r6));
  LED led_88 (.in(column_7_p2r6));
  LED led_89 (.in(column_7_p1r5));
  LED led_90 (.in(column_7_p2r5));
  LED led_91 (.in(column_7_p1r4));
  LED led_92 (.in(column_7_p2r4));
  LED led_93 (.in(column_7_p1r3));
  LED led_94 (.in(column_7_p2r3));
  LED led_95 (.in(column_7_p1r2));
  LED led_96 (.in(column_7_p2r2));
  LED led_97 (.in(column_7_p1r1));
  LED led_98 (.in(column_7_p2r1));
  LED led_99 (.in(column_7_p1r0));
  LED led_100 (.in(column_7_p2r0));
  or _7_2 (_7_2_out, and_6_out, and_13_out);
  Button _5_3 (.out(_5_3_out));
  Button _6_3 (.out(_6_3_out));
  Button _4_3 (.out(_4_3_out));
  and and_11 (and_11_out, _4_3_out, sr_flip_flop_1_minus_q);
  and and_12 (and_12_out, _5_3_out, sr_flip_flop_1_minus_q);
  Button _7_3 (.out(_7_3_out));
  and and_13 (and_13_out, _7_3_out, sr_flip_flop_1_minus_q);
  and and_14 (and_14_out, _6_3_out, sr_flip_flop_1_minus_q);

  // Notes on the sheet:
  //   Player 1
  //   Connect 4
  //   Player 2
endmodule

module Column (
  input  clock,
  input  reset,
  input  player_2,
  input  player_1,
  output p1r6,
  output p2r6,
  output p1r5,
  output p2r5,
  output p1r4,
  output p2r4,
  output p1r3,
  output p2r3,
  output p1r2,
  output p2r2,
  output p1r1,
  output p2r1,
  output p1r0,
  output p2r0
);

  wire n3_bit_counter_1_o0, n3_bit_counter_1_o1, n3_bit_counter_1_o2, n3_bit_decoder_1_out_4,
       n3_bit_decoder_1_out_5, n3_bit_decoder_1_out_6, n3_bit_decoder_1_out_7, n3_bit_decoder_1_out_8,
       n3_bit_decoder_1_out_9, n3_bit_decoder_1_out_10, not_1_out, not_2_out, not_3_out, or_1_out, or_2_out,
       or_3_out, or_4_out, or_5_out, or_6_out, sr_flip_flop_1_minus_q, sr_flip_flop_1_q;

  _3_bit_Counter u_3_bit_counter_1 (
    .Clock(clock), .Reset(reset), .o0(n3_bit_counter_1_o0), .o1(n3_bit_counter_1_o1), .o2(n3_bit_counter_1_o2));
  not not_1 (not_1_out, n3_bit_counter_1_o0);
  not not_2 (not_2_out, n3_bit_counter_1_o1);
  not not_3 (not_3_out, n3_bit_counter_1_o2);
  _3_bit_Decoder u_3_bit_decoder_1 (
    .a2(not_3_out), .a1(not_2_out), .a0(not_1_out), .out_4(n3_bit_decoder_1_out_4),
    .out_5(n3_bit_decoder_1_out_5), .out_6(n3_bit_decoder_1_out_6), .out_7(n3_bit_decoder_1_out_7),
    .out_8(n3_bit_decoder_1_out_8), .out_9(n3_bit_decoder_1_out_9), .out_10(n3_bit_decoder_1_out_10));  // open: out_11
  SR_Flip_Flop sr_flip_flop_1 (.R(player_1), .S(player_2), .Q(sr_flip_flop_1_q), .minus_Q(sr_flip_flop_1_minus_q));
  Node node_1 (
    .Clock(n3_bit_decoder_1_out_4), .player1(sr_flip_flop_1_minus_q), .player2(sr_flip_flop_1_q),
    .reset(reset), .player1output(p1r6), .player2output(p2r6));
  or or_1 (or_1_out, n3_bit_decoder_1_out_4, n3_bit_decoder_1_out_5);
  or or_2 (or_2_out, or_1_out, n3_bit_decoder_1_out_6);
  Node node_2 (
    .Clock(or_1_out), .player1(sr_flip_flop_1_minus_q), .player2(sr_flip_flop_1_q), .reset(reset),
    .player1output(p1r5), .player2output(p2r5));
  or or_3 (or_3_out, or_2_out, n3_bit_decoder_1_out_7);
  or or_4 (or_4_out, or_3_out, n3_bit_decoder_1_out_8);
  or or_5 (or_5_out, or_4_out, n3_bit_decoder_1_out_9);
  or or_6 (or_6_out, or_5_out, n3_bit_decoder_1_out_10);
  Node node_3 (
    .Clock(or_2_out), .player1(sr_flip_flop_1_minus_q), .player2(sr_flip_flop_1_q), .reset(reset),
    .player1output(p1r4), .player2output(p2r4));
  Node node_4 (
    .Clock(or_3_out), .player1(sr_flip_flop_1_minus_q), .player2(sr_flip_flop_1_q), .reset(reset),
    .player1output(p1r3), .player2output(p2r3));
  Node node_5 (
    .Clock(or_4_out), .player1(sr_flip_flop_1_minus_q), .player2(sr_flip_flop_1_q), .reset(reset),
    .player1output(p1r2), .player2output(p2r2));
  Node node_6 (
    .Clock(or_5_out), .player1(sr_flip_flop_1_minus_q), .player2(sr_flip_flop_1_q), .reset(reset),
    .player1output(p1r1), .player2output(p2r1));
  Node node_7 (
    .Clock(or_6_out), .player1(sr_flip_flop_1_minus_q), .player2(sr_flip_flop_1_q), .reset(reset),
    .player1output(p1r0), .player2output(p2r0));

  // Notes on the sheet:
  //   Column logic
endmodule

module Node (
  input  player1,
  input  player2,
  input  reset,
  input  Clock,
  output player1output,
  output player2output
);

  wire and_1_out, and_2_out, sr_flip_flop_1_q, sr_flip_flop_2_q;

  and and_1 (and_1_out, player1, sr_flip_flop_2_q, Clock);
  and and_2 (and_2_out, player2, sr_flip_flop_1_q, Clock);
  SR_Flip_Flop sr_flip_flop_1 (.R(and_1_out), .S(reset), .Q(sr_flip_flop_1_q), .minus_Q(player1output));
  SR_Flip_Flop sr_flip_flop_2 (.R(and_2_out), .S(reset), .Q(sr_flip_flop_2_q), .minus_Q(player2output));

  // Notes on the sheet:
  //   Node logic
  //   Changes the state of the node according to the player who took the turn.
  //   After a set, no further sets are possible. Use reset to reset.
endmodule

// Counter
module _3_bit_Counter (
  input  Clock,
  input  Reset,
  output o0,
  output o1,
  output o2
);

  wire and_1_out, or_1_out;

  or or_1 (or_1_out, Clock, Reset);
  J_K_Flip_Flop j_k_ff_1 (.J(1'b1), .clk(or_1_out), .K(1'b1), .Q(o0), .reset(Reset));  // open: Qn, preset, en
  J_K_Flip_Flop j_k_ff_2 (.J(o0), .clk(or_1_out), .K(o0), .Q(o1), .reset(Reset));  // open: Qn, preset, en
  and and_1 (and_1_out, o1, o0);
  J_K_Flip_Flop j_k_ff_3 (.J(and_1_out), .clk(or_1_out), .K(and_1_out), .Q(o2), .reset(Reset));  // open: Qn, preset, en

  // Notes on the sheet:
  //   3 bit Counter
endmodule

// Decoder
module _3_bit_Decoder (
  input  a2,
  input  a1,
  input  a0,
  output out_4,
  output out_5,
  output out_6,
  output out_7,
  output out_8,
  output out_9,
  output out_10,
  output out_11
);

  wire not_1_out, not_2_out, not_3_out;

  not not_1 (not_1_out, a2);
  not not_2 (not_2_out, a0);
  not not_3 (not_3_out, a1);
  and and_1 (out_4, not_1_out, not_3_out, not_2_out);
  and and_2 (out_5, not_1_out, not_3_out, a0);
  and and_3 (out_6, not_1_out, a1, not_2_out);
  and and_4 (out_7, not_1_out, a1, a0);
  and and_5 (out_8, a2, not_3_out, not_2_out);
  and and_6 (out_9, a2, not_3_out, a0);
  and and_7 (out_10, a2, a1, not_2_out);
  and and_8 (out_11, a2, a1, a0);

  // Notes on the sheet:
  //   3 bit Decoder
endmodule

module SR_Flip_Flop (
  input  R,
  input  S,
  output Q,
  output minus_Q
);

  nor nor_1 (Q, R, minus_Q);
  nor nor_2 (minus_Q, Q, S);

  // Notes on the sheet:
  //   S-R Flip-Flop
endmodule
